# Fritzing sketch mk1 (saved by Fritzing 0.9.2b)
breadboards: 1

parts:
  TRINKET1 = Trinket 5V
  J1 = Basic Force Sensing Resistor (FSR) [package=THT]
  J2 = Piezo Speaker
  J3 = female pin header, 2 pins [form="♀ (female)"]
  R1 = Resistor [tolerance=±5% resistance=680k package=THT]

nets:
  N1: TRINKET1.no_name_yet#1, J3.pin2
  N2: TRINKET1.no_name_yet#2, J2.pin1, J3.pin1, R1.Pin_0
  N3: TRINKET1.no_name_yet#6, J1.pin_0
  N4: TRINKET1.no_name_yet#7, J1.pin_1, R1.Pin_1
  N5: TRINKET1.no_name_yet#9, J2.pin2

custom parts:
  Trinket 5V: Adafruit Trinket 5V
